// Logisim project 16-bit.circ as structural Verilog
module _4_bit_ALU (
  input  [3:0] A,
  input  [3:0] B,
  input  [1:0] ALU_Op,
  output [3:0] ALU_Out
);

  wire and_1_out;
  wire [3:0] adder_1_out, and_2_out, multiplexer_1_out, not_1_out, or_1_out;

  Multiplexer #(.width(4), .enable("false")) multiplexer_1 (
    .in0(B), .in1(not_1_out), .out(multiplexer_1_out), .sel(and_1_out));
  assign not_1_out = ~B;  // NOT_Gate not_1, 4 bits wide
  and and_1 (and_1_out, ALU_Op[0], ALU_Op[1]);
  Adder #(.width(4)) adder_1 (.a(A), .b(multiplexer_1_out), .out(adder_1_out), .cin(and_1_out));  // open: cout
  assign and_2_out = multiplexer_1_out & A;  // AND_Gate and_2, 4 bits wide
  assign or_1_out = multiplexer_1_out | A;  // OR_Gate or_1, 4 bits wide
  Multiplexer #(.select(2), .width(4), .enable("false")) multiplexer_2 (
    .in0(adder_1_out), .in1(and_2_out), .in2(or_1_out), .in3(adder_1_out), .out(ALU_Out), .sel(ALU_Op));

  // Notes on the sheet:
  //   4 Bit ALU
  //   00 = ADD
  //   01 = AND
  //   10 = OR
  //   11 = SUB
  //   sub not B
  //   sub cin
  //   sub
endmodule

module _16x8_bit_Register_File (
  input  [7:0] Data_In,
  input  WE,
  input  [3:0] Read_Addr_1,
  input  Clock,
  input  [3:0] Read_Addr_2,
  input  [3:0] Write_Addr,
  output [7:0] Read_1_Data,
  output [7:0] Read_2_Data
);

  wire demultiplexer_1_out0, demultiplexer_1_out1, demultiplexer_1_out2, demultiplexer_1_out3,
       demultiplexer_1_out4, demultiplexer_1_out5, demultiplexer_1_out6, demultiplexer_1_out7,
       demultiplexer_1_out8, demultiplexer_1_out9, demultiplexer_1_out10, demultiplexer_1_out11,
       demultiplexer_1_out12, demultiplexer_1_out13, demultiplexer_1_out14, demultiplexer_1_out15;
  wire [7:0] register_1_q, register_2_q, register_3_q, register_4_q, register_5_q, register_6_q,
       register_7_q, register_8_q, register_9_q, register_10_q, register_11_q, register_12_q, register_13_q,
       register_14_q, register_15_q, register_16_q;

  Demultiplexer #(.select(4), .enable("false")) demultiplexer_1 (
    .out0(demultiplexer_1_out0), .out1(demultiplexer_1_out1), .out2(demultiplexer_1_out2),
    .out3(demultiplexer_1_out3), .out4(demultiplexer_1_out4), .out5(demultiplexer_1_out5),
    .out6(demultiplexer_1_out6), .out7(demultiplexer_1_out7), .out8(demultiplexer_1_out8),
    .out9(demultiplexer_1_out9), .out10(demultiplexer_1_out10), .out11(demultiplexer_1_out11),
    .out12(demultiplexer_1_out12), .out13(demultiplexer_1_out13), .out14(demultiplexer_1_out14),
    .out15(demultiplexer_1_out15), .in(WE), .sel(Write_Addr));
  Register register_1 (.D(Data_In), .en(demultiplexer_1_out0), .Q(register_1_q), .clk(Clock));  // open: clr
  Register register_2 (.D(Data_In), .en(demultiplexer_1_out1), .Q(register_2_q), .clk(Clock));  // open: clr
  Register register_3 (.D(Data_In), .en(demultiplexer_1_out2), .Q(register_3_q), .clk(Clock));  // open: clr
  Register register_4 (.D(Data_In), .en(demultiplexer_1_out3), .Q(register_4_q), .clk(Clock));  // open: clr
  Register register_5 (.D(Data_In), .en(demultiplexer_1_out4), .Q(register_5_q), .clk(Clock));  // open: clr
  Register register_6 (.D(Data_In), .en(demultiplexer_1_out5), .Q(register_6_q), .clk(Clock));  // open: clr
  Register register_7 (.D(Data_In), .en(demultiplexer_1_out6), .Q(register_7_q), .clk(Clock));  // open: clr
  Register register_8 (.D(Data_In), .en(demultiplexer_1_out7), .Q(register_8_q), .clk(Clock));  // open: clr
  Register register_9 (.D(Data_In), .en(demultiplexer_1_out8), .Q(register_9_q), .clk(Clock));  // open: clr
  Register register_10 (.D(Data_In), .en(demultiplexer_1_out9), .Q(register_10_q), .clk(Clock));  // open: clr
  Register register_11 (.D(Data_In), .en(demultiplexer_1_out10), .Q(register_11_q), .clk(Clock));  // open: clr
  Register register_12 (.D(Data_In), .en(demultiplexer_1_out11), .Q(register_12_q), .clk(Clock));  // open: clr
  Register register_13 (.D(Data_In), .en(demultiplexer_1_out12), .Q(register_13_q), .clk(Clock));  // open: clr
  Register register_14 (.D(Data_In), .en(demultiplexer_1_out13), .Q(register_14_q), .clk(Clock));  // open: clr
  Register register_15 (.D(Data_In), .en(demultiplexer_1_out14), .Q(register_15_q), .clk(Clock));  // open: clr
  Register register_16 (.D(Data_In), .en(demultiplexer_1_out15), .Q(register_16_q), .clk(Clock));  // open: clr
  Multiplexer #(.select(4), .width(8), .enable("false")) multiplexer_1 (
    .in0(register_1_q), .in1(register_2_q), .in2(register_3_q), .in3(register_4_q), .in4(register_5_q),
    .in5(register_6_q), .in6(register_7_q), .in7(register_8_q), .in8(register_9_q), .in9(register_10_q),
    .in10(register_11_q), .in11(register_12_q), .in12(register_13_q), .in13(register_14_q),
    .in14(register_15_q), .in15(register_16_q), .out(Read_1_Data), .sel(Read_Addr_1));
  Multiplexer #(.select(4), .width(8), .enable("false")) multiplexer_2 (
    .in0(register_1_q), .in1(register_2_q), .in2(register_3_q), .in3(register_4_q), .in4(register_5_q),
    .in5(register_6_q), .in6(register_7_q), .in7(register_8_q), .in8(register_9_q), .in9(register_10_q),
    .in10(register_11_q), .in11(register_12_q), .in12(register_13_q), .in13(register_14_q),
    .in14(register_15_q), .in15(register_16_q), .out(Read_2_Data), .sel(Read_Addr_2));

  // Notes on the sheet:
  //   16x8-bit Register File
endmodule

module ALU_REG_Instruction (
  input  [13:0] in_1,
  input  clock,
  output [3:0] CPU_Op_Out
);

  wire [3:0] bit_extender_1_out, multiplexer_1_out, n16x8_bit_register_file_1_p7,
       n16x8_bit_register_file_1_p8;

  // _16x8_bit_Register_File 16x8_bit_register_file_1: pin names not known; wires that end beside it: CPU_Op_Out, 1'b1, clock, in_1[8:6], in_1[5:3], in_1[2:0], n16x8_bit_register_file_1_p7, n16x8_bit_register_file_1_p8
  Multiplexer #(.width(4), .enable("false")) multiplexer_1 (
    .in0(n16x8_bit_register_file_1_p8), .in1(bit_extender_1_out), .out(multiplexer_1_out), .sel(in_1[13]));
  assign bit_extender_1_out = {{1{in_1[2]}}, in_1[2:0]};  // Bit_Extender bit_extender_1
  _4_bit_ALU u_4_bit_alu_1 (
    .A(n16x8_bit_register_file_1_p7), .B(multiplexer_1_out), .ALU_Op(in_1[10:9]), .ALU_Out(CPU_Op_Out));

  // Notes on the sheet:
  //   op
  //   src2
  //   src1
  //   immed data
  //   immed select
  //   ALU op
  //   dest
endmodule

module ALU_With_Mem (
  input  [13:0] in_1,
  input  clock,
  output [3:0] out_3,
  output [3:0] CPU_Op_Out
);

  wire not_1_out;
  wire [2:0] multiplexer_1_out;
  wire [3:0] bit_extender_1_out, multiplexer_2_out, n16x8_bit_register_file_1_p7,
       n16x8_bit_register_file_1_p8, ram_1_data;

  not not_1 (not_1_out, in_1[12]);
  Multiplexer #(.width(3), .enable("false")) multiplexer_1 (
    .in0(in_1[2:0]), .in1(in_1[8:6]), .out(multiplexer_1_out), .sel(in_1[12]));
  // _16x8_bit_Register_File 16x8_bit_register_file_1: pin names not known; wires that end beside it: out_3, not_1_out, clock, in_1[8:6], in_1[5:3], multiplexer_1_out, n16x8_bit_register_file_1_p7, n16x8_bit_register_file_1_p8
  Multiplexer #(.width(4), .enable("false")) multiplexer_2 (
    .in0(n16x8_bit_register_file_1_p8), .in1(bit_extender_1_out), .out(multiplexer_2_out), .sel(in_1[13]));
  assign bit_extender_1_out = {{1{in_1[2]}}, in_1[2:0]};  // Bit_Extender bit_extender_1
  Multiplexer #(.width(4), .enable("false")) multiplexer_3 (
    .in0(CPU_Op_Out), .in1(ram_1_data), .out(out_3), .sel(in_1[11]));
  _4_bit_ALU u_4_bit_alu_1 (
    .A(n16x8_bit_register_file_1_p7), .B(multiplexer_2_out), .ALU_Op(in_1[10:9]), .ALU_Out(CPU_Op_Out));
  RAM #(.addrWidth(4), .dataWidth(4), .bus("separate")) ram_1 (
    .addr(CPU_Op_Out), .din(n16x8_bit_register_file_1_p8), .data(ram_1_data), .str(in_1[12]), .sel(1'b1),
    .clk(clock), .ld(in_1[11]), .clr(1'b0));

  // Notes on the sheet:
  //   op
  //   src2
  //   src1
  //   immed data
  //   immed select
  //   ALU op
  //   dest
endmodule

module ALU_With_Mem___CLU (
  input  [13:0] in_1,
  input  clock,
  output [3:0] CPU_Op_Out
);

  wire control_logic_1_p2, control_logic_1_p3, control_logic_1_p4, control_logic_1_p5, control_logic_1_p6,
       control_logic_1_p7, control_logic_1_p8, n16x8_bit_register_file_1_p7;
  wire [2:0] n16x8_bit_register_file_1_p6;
  wire [3:0] bit_extender_1_out, multiplexer_2_out, n16x8_bit_register_file_1_p1,
       n16x8_bit_register_file_1_p8, ram_1_data;

  // Control_Logic control_logic_1: pin names not known; wires that end beside it: in_1[13:9], control_logic_1_p2, control_logic_1_p3, control_logic_1_p4, control_logic_1_p5, control_logic_1_p6, control_logic_1_p7, control_logic_1_p8
  // _16x8_bit_Register_File 16x8_bit_register_file_1: pin names not known; wires that end beside it: n16x8_bit_register_file_1_p1, control_logic_1_p2, clock, in_1[8:6], in_1[5:3], n16x8_bit_register_file_1_p6, n16x8_bit_register_file_1_p7, n16x8_bit_register_file_1_p8
  Multiplexer #(.width(3), .enable("false")) multiplexer_1 (
    .in0(in_1[2:0]), .in1(in_1[8:6]), .out(n16x8_bit_register_file_1_p6), .sel(control_logic_1_p3));
  assign bit_extender_1_out = {{1{in_1[2]}}, in_1[2:0]};  // Bit_Extender bit_extender_1
  Multiplexer #(.width(4), .enable("false")) multiplexer_2 (
    .in0(n16x8_bit_register_file_1_p8), .in1(bit_extender_1_out), .out(multiplexer_2_out),
    .sel(control_logic_1_p4));
  Multiplexer #(.width(4), .enable("false")) multiplexer_3 (
    .in0(CPU_Op_Out), .in1(ram_1_data), .out(n16x8_bit_register_file_1_p1), .sel(control_logic_1_p6));
  // _4_bit_ALU 4_bit_alu_1: pin names not known; wires that end beside it: n16x8_bit_register_file_1_p7, multiplexer_2_out, control_logic_1_p8, CPU_Op_Out
  RAM #(.addrWidth(4), .dataWidth(4), .bus("separate")) ram_1 (
    .addr(CPU_Op_Out), .din(n16x8_bit_register_file_1_p8), .data(ram_1_data), .str(control_logic_1_p5),
    .sel(1'b1), .clk(clock), .ld(control_logic_1_p7), .clr(1'b0));

  // Notes on the sheet:
  //   op
  //   dest
  //   src2
  //   IMM Din
  //   IMM sel
  //   SW
  //   ALU/RAM MUX
  //   LW
  //   ALU op
  //   clock
endmodule

module Control_Logic (
  input  [7:0] opcode,
  output JMP,
  output WE,
  output SRC2_DEST_MUX,
  output IMM_RA2_MUX,
  output SW,
  output ALU_RAM_MUX,
  output LW,
  output [3:0] OP
);

  nor nor_1 (WE, opcode[4], opcode[6]);

  assign ALU_RAM_MUX = opcode[5];
  assign IMM_RA2_MUX = opcode[7];
  assign JMP = opcode[4];
  assign LW = opcode[5];
  assign OP = opcode[3:0];
  assign SRC2_DEST_MUX = opcode[6];
  assign SW = opcode[6];
endmodule

module Program_Counter (
  input  [7:0] JMP_ADDR,
  input  JMP,
  input  clock,
  input  reset,
  output [7:0] Instruction_Pointer
);

  wire [7:0] multiplexer_1_out, n8_bit_alu_1_alu_out;

  Multiplexer #(.width(8), .enable("false")) multiplexer_1 (
    .in0(n8_bit_alu_1_alu_out), .in1(JMP_ADDR), .out(multiplexer_1_out), .sel(JMP));
  Register Program_Counter (.D(multiplexer_1_out), .en(1'b1), .Q(Instruction_Pointer), .clk(clock), .clr(reset));
  _8_bit_ALU u_8_bit_alu_1 (.A(Instruction_Pointer), .B(8'h1), .ALU_Op(4'b0000), .ALU_Out(n8_bit_alu_1_alu_out));
endmodule

module _8_bit_ALU (
  input  [7:0] A,
  input  [7:0] B,
  input  [3:0] ALU_Op,
  output [7:0] ALU_Out
);

  wire and_1_out;
  wire [7:0] adder_1_out, and_2_out, multiplexer_1_out, not_1_out, or_1_out;

  Multiplexer #(.width(8), .enable("false")) multiplexer_1 (
    .in0(B), .in1(not_1_out), .out(multiplexer_1_out), .sel(and_1_out));
  assign not_1_out = ~B;  // NOT_Gate not_1, 8 bits wide
  and and_1 (and_1_out, ALU_Op[0], ALU_Op[1]);
  Adder adder_1 (.a(A), .b(multiplexer_1_out), .out(adder_1_out), .cin(and_1_out));  // open: cout
  assign and_2_out = multiplexer_1_out & A;  // AND_Gate and_2, 8 bits wide
  assign or_1_out = multiplexer_1_out | A;  // OR_Gate or_1, 8 bits wide
  Multiplexer #(.select(2), .width(8), .enable("false")) multiplexer_2 (
    .in0(adder_1_out), .in1(and_2_out), .in2(or_1_out), .in3(adder_1_out), .out(ALU_Out), .sel(ALU_Op[1:0]));

  // Notes on the sheet:
  //   Other operations
  //   8 Bit ALU
  //   00 = ADD
  //   01 = AND
  //   10 = OR
  //   11 = SUB
  //   coming soon™
  //   sub not B
  //   sub cin
  //   sub
endmodule

module Truncator (
  input  [7:0] Input,
  output [3:0] Output
);


  assign Output = Input[3:0];
endmodule

module Full_CPU (
  output [7:0] CPU_Op_Out
);

  wire CLK, control_logic_1_alu_ram_mux, control_logic_1_imm_ra2_mux, control_logic_1_jmp,
       control_logic_1_lw, control_logic_1_src2_dest_mux, control_logic_1_sw, control_logic_1_we;
  wire [3:0] control_logic_1_op, multiplexer_1_out, truncator_1_output;
  wire [7:0] multiplexer_2_out, multiplexer_3_out, n16x8_bit_register_file_1_read_1_data,
       n16x8_bit_register_file_1_read_2_data, PC_instruction_pointer, ram_2_data;
  wire [23:0] ram_1_data;

  Clock Clock (.out(CLK));
  Program_Counter PC (
    .JMP_ADDR(multiplexer_2_out), .Instruction_Pointer(PC_instruction_pointer), .JMP(control_logic_1_jmp),
    .clock(CLK), .reset(1'b0));
  RAM #(.dataWidth(24), .bus("separate")) ram_1 (
    .addr(PC_instruction_pointer), .data(ram_1_data), .str(1'b0), .sel(1'b1), .clk(CLK), .ld(1'b1), .clr(1'b0));  // open: din
  Control_Logic control_logic_1 (
    .opcode(ram_1_data[23:16]), .JMP(control_logic_1_jmp), .WE(control_logic_1_we),
    .SRC2_DEST_MUX(control_logic_1_src2_dest_mux), .IMM_RA2_MUX(control_logic_1_imm_ra2_mux),
    .SW(control_logic_1_sw), .ALU_RAM_MUX(control_logic_1_alu_ram_mux), .LW(control_logic_1_lw),
    .OP(control_logic_1_op));
  Truncator truncator_1 (.Input(ram_1_data[7:0]), .Output(truncator_1_output));
  Multiplexer #(.width(4), .enable("false")) multiplexer_1 (
    .in0(truncator_1_output), .in1(ram_1_data[15:12]), .out(multiplexer_1_out),
    .sel(control_logic_1_src2_dest_mux));
  _16x8_bit_Register_File u_16x8_bit_register_file_1 (
    .Data_In(multiplexer_3_out), .WE(control_logic_1_we), .Clock(CLK), .Write_Addr(ram_1_data[15:12]),
    .Read_Addr_1(ram_1_data[11:8]), .Read_Addr_2(multiplexer_1_out),
    .Read_1_Data(n16x8_bit_register_file_1_read_1_data), .Read_2_Data(n16x8_bit_register_file_1_read_2_data));
  Multiplexer #(.width(8), .enable("false")) multiplexer_2 (
    .in0(n16x8_bit_register_file_1_read_2_data), .in1(ram_1_data[7:0]), .out(multiplexer_2_out),
    .sel(control_logic_1_imm_ra2_mux));
  Multiplexer #(.width(8), .enable("false")) multiplexer_3 (
    .in0(CPU_Op_Out), .in1(ram_2_data), .out(multiplexer_3_out), .sel(control_logic_1_alu_ram_mux));
  _8_bit_ALU u_8_bit_alu_1 (
    .A(n16x8_bit_register_file_1_read_1_data), .B(multiplexer_2_out), .ALU_Op(control_logic_1_op),
    .ALU_Out(CPU_Op_Out));
  RAM #(.bus("separate")) ram_2 (
    .addr(CPU_Op_Out), .din(n16x8_bit_register_file_1_read_2_data), .data(ram_2_data),
    .str(control_logic_1_sw), .sel(1'b1), .clk(CLK), .ld(control_logic_1_lw), .clr(1'b0));

  // Notes on the sheet:
  //   Instruction Memory
  //   op
  //   SRC1
  //   WA
  //   IMMV/SRC2
  //   IMM sel
  //   SW
  //   ALU/RAM MUX
  //   LW
  //   ALU op
  //   clock
  //   Register File
  //   SRC2/DEST
  //   IMM/RA2
  //   ALU/RAM
  //   Data Memory
endmodule
